# Fritzing sketch schematicWemos (saved by Fritzing 1.0.0rc)
breadboards: 1

parts:
  Part1 = HX711 Weighing Sensor Module
  IC1 = ULN2003A [package="SO16 [SMD]"]
  S3 = Pushbutton [package="[THT]"]
  Piezo_buzzer1 = Piezo Buzzer
  MOTOR1 = Vibration Motor
  LED1 = LED - 5mm [color="Red (633nm)" current=0.030A package="5 mm [THT]"]
  S4 = Load Sensor - 50kg [part_number=SEN-10245]
  R2 = Resistor [tolerance=±5% resistance=1k package="0805 [SMD]"]
  R3 = Resistor [tolerance=±5% resistance=1k package="0805 [SMD]"]
  WeMos_D1_Mini1 = WeMos D1 Mini

nets:
  N1: Part1.E+, S4.W, R3.Pin_0
  N2: Part1.E-, S4.B, R2.Pin_0
  N3: Part1.A+, R2.Pin_1, R3.Pin_1
  N4: Part1.A-, S4.R
  N5: IC1.In_1, WeMos_D1_Mini1.D5
  N6: IC1.In_2, WeMos_D1_Mini1.D6
  N7: IC1.In_3, WeMos_D1_Mini1.D7
  N8: IC1.0V, Piezo_buzzer1.pin_1, MOTOR1.NEG, LED1.cathode, WeMos_D1_Mini1.5V
  N9: IC1.COM_-_Common, WeMos_D1_Mini1.G
  N10: IC1.Out_3, MOTOR1.POS
  N11: IC1.Out_2, LED1.anode
  N12: IC1.Out_1, Piezo_buzzer1.pin_2
  N13: S3.Pin_1, S3.Pin_2, WeMos_D1_Mini1.3V3
  N14: S3.Pin_3, S3.Pin_4, WeMos_D1_Mini1.D3

notes:
  +5V
  GND
  You can power the entire board either through the MicroUSB port on the Wemos module or via the 5V and G (GND) pins.

custom parts:
  HX711 Weighing Sensor Module: HX711 is a precision 24-bit analog-to-digital converter (ADC) designed for weigh scales and industrial control applications to interface directly with a bridge sensor.
  Piezo Buzzer: Piezo buzzer PS1420P02CT
  Vibration Motor: An eccentric vibration motor!
  Load Sensor - 50kg: Half-wheatstone bridge Load Cell modified from the Fritzing Repo This load sensor, sometimes called a strain gauge, is the same one found in digital bathroom scales (you know, the ones you use in January for your New Year's resolutions, and then forget about a month later). This sensor can measure up to about 110 pounds.
